// Logisim project LogisimProj1Pt.1.circ as structural Verilog: 1 circuit, main circuit main
module main (
  input  A,
  input  B,
  input  C
);

  wire and_1_out, and_2_out, and_3_out, and_4_out, and_5_out, and_7_out, not_1_out, not_2_out, not_3_out,
       or_1_out, undriven, undriven_2, undriven_3;

  not not_1 (not_1_out, B);
  not not_2 (not_2_out, A);
  not not_3 (not_3_out, C);
  and and_1 (and_1_out, C, B, A);
  and and_2 (and_2_out, not_2_out, B, C);
  and and_3 (and_3_out, A, not_1_out, not_3_out);
  and and_4 (and_4_out, A, not_1_out, C);
  and and_5 (and_5_out, not_2_out, not_1_out, C);
  or or_1 (or_1_out, and_1_out, and_2_out, and_3_out, and_4_out, and_5_out);
  LED led_1 (.in(or_1_out));
  // AND_Gate and_6 is placed but not wired
  and and_7 (and_7_out, undriven, undriven_2, undriven_3);
  and and_8 (and_7_out, undriven, undriven_2, undriven_3);

  // Notes on the sheet:
  //   F(A,B,C) = ABC+A’BC+AB’C’+AB’C+A’B’C
endmodule
