// Logisim project LogisimProject1Pt2.circ as structural Verilog: 1 circuit, main circuit main
module main (
  input  A,
  input  B,
  input  C
);

  wire nand_1_out, nand_2_out, nand_3_out, nand_4_out, nand_5_out, nand_6_out, nand_8_out, nand_10_out,
       nand_12_out;

  nand nand_1 (nand_1_out, B, B);
  nand nand_2 (nand_2_out, A, A);
  nand nand_3 (nand_3_out, C, C);
  nand nand_4 (nand_4_out, A, B, C);
  nand nand_5 (nand_5_out, nand_2_out, B, C);
  nand nand_6 (nand_6_out, A, nand_1_out, nand_3_out);
  nand nand_7 (nand_6_out, A, nand_1_out, nand_3_out);
  nand nand_8 (nand_8_out, A, nand_1_out, C);
  nand nand_9 (nand_8_out, A, nand_1_out, C);
  nand nand_10 (nand_10_out, nand_2_out, nand_1_out, C);
  nand nand_11 (nand_10_out, nand_2_out, nand_1_out, C);
  nand nand_12 (nand_12_out, nand_4_out, nand_5_out, nand_6_out, nand_8_out, nand_10_out);
  LED led_1 (.in(nand_12_out));

  // Notes on the sheet:
  //   F(A,B,C)= ((ABC)'(A'BC)'(AB'C')'(AB'C)(A'B'C)')'
endmodule
